# Fritzing sketch Esp8266_Cizim (saved by Fritzing 0.8.7b)
breadboards: 1

parts:
  U1 = ESP8266 WiFi Module [part_number=ESP8266]
  Part1 = Arduino Uno (Rev3)

nets:
  N1: U1.RXD, Part1.D0/RX
  VCC: U1.VCC, U1.CH_PD, Part1.3V3
  GND: U1.GPIO_0, U1.GND, Part1.GND

custom parts:
  ESP8266 WiFi Module: Generic WiFi Module based on the ESP8266 with onboard PCB antenna and UART communications
